// Digital circuit 6502.dig as structural Verilog
module _6502 (
  input  Clock,
  input  [2:0] ALU_Control,
  input  Reset,
  input  [15:0] Addr_In,
  input  Inc,
  input  Dec,
  input  Jump,
  input  Count,
  input  [1:0] Chip_Select,
  input  R_W,
  input  Addr_IO,
  input  En,
  input  En_2,
  input  [7:0] Data,
  input  [7:0] Data_2,
  output Zero,
  output Carry,
  output [7:0] Data_Out,
  output [15:0] Addr_Out,
  output out_13,
  output out_15
);

  wire PC_CS, SP_CS;
  wire [7:0] A_q, B_q;
  wire [15:0] driver_1_out;

  Decoder #(.Selector_Bits(2)) decoder_1 (.sel(Chip_Select), .out_0(PC_CS), .out_1(SP_CS));  // open: out_2, out_3
  StackPointer_6502 stackpointer_6502_1 ();
  ProgramCounter_6502 programcounter_6502_1 ();
  assign driver_1_out = Addr_IO ? Addr_In : 16'bz;  // Driver driver_1
  assign Addr_Out = ~Addr_IO ? driver_1_out : 16'bz;  // DriverInvSel driverinvsel_1
  Register #(.Bits(8)) A (.D(Data), .C(Clock), .en(En_2), .Q(A_q));
  ALU_6502 alu_6502_1 ();
  Register #(.Bits(8)) B (.D(Data_2), .C(Clock), .en(En), .Q(B_q));
endmodule
